// Logisim project CPU.circ as structural Verilog: 2 circuits, main circuit main
module main (
  input  in_1
);

  wire and_1_out, and_2_out, and_3_out, and_4_out, and_5_out, and_6_out, and_7_out, and_8_out, and_9_out,
       and_10_out, and_11_out, and_12_out, and_13_out, and_14_out, and_15_out, and_16_out, and_17_out,
       and_19_out, and_20_out, and_21_out, and_22_out, and_26_out, clock_1_out, decoder_1_out0,
       decoder_1_out1, decoder_1_out2, decoder_1_out3, decoder_2_out0, decoder_2_out1, decoder_2_out2,
       decoder_2_out3, decoder_3_out0, decoder_3_out1, decoder_3_out2, decoder_3_out3, decoder_3_out4,
       decoder_3_out5, decoder_3_out6, decoder_3_out7, not_1_out, not_2_out, not_3_out, or_1_out, or_2_out,
       or_3_out, or_4_out, or_5_out, or_6_out, or_7_out;
  wire [3:0] controlled_buffer_2_out, counter_2_q, register_1_q, register_2_q, register_6_q_2;
  wire [7:0] alu_8bit_1_c0, controlled_buffer_1_out, controlled_buffer_3_out, counter_1_q, ram_1_data,
       register_3_q, register_4_q, register_5_q, register_7_q, rom_1_data;
  wire [7:4] controlled_buffer_2_out_2, register_6_q;

  Clock clock_1 (.out(clock_1_out));
  Counter #(.max('hb)) counter_1 (.Q(counter_1_q), .clk(clock_1_out), .clr(in_1));  // open: load, D, count, carry
  assign controlled_buffer_1_out = or_6_out ? rom_1_data : 8'bz;  // Controlled_Buffer controlled_buffer_1
  Counter #(.width(4), .max('hf)) counter_2 (
    .Q(counter_2_q), .clk(clock_1_out), .clr(or_1_out));  // open: load, D, count, carry
  or or_1 (or_1_out, in_1, decoder_1_out3);
  not not_1 (not_1_out, and_1_out);
  and and_1 (and_1_out, clock_1_out, and_17_out);
  Decoder #(.select(4)) decoder_1 (
    .out0(decoder_1_out0), .out1(decoder_1_out1), .out2(decoder_1_out2), .out3(decoder_1_out3),
    .sel(counter_2_q));  // open: out4, out5, out6, out7, out8, out9, out10, out11, out12, out13, out14, out15, en
  ROM rom_1 (.addr(counter_1_q), .data(rom_1_data));  // open: sel
  assign {controlled_buffer_2_out_2, controlled_buffer_2_out} = or_4_out ? rom_1_data : 8'bz;  // Controlled_Buffer controlled_buffer_2
  Register #(.width(4)) register_1 (
    .D(controlled_buffer_2_out), .Q(register_1_q), .clk(or_7_out), .clr(in_1));  // open: en
  Decoder #(.select(4)) decoder_2 (
    .out0(decoder_2_out0), .out1(decoder_2_out1), .out2(decoder_2_out2), .out3(decoder_2_out3),
    .sel(register_1_q));  // open: out4, out5, out6, out7, out8, out9, out10, out11, out12, out13, out14, out15, en
  RAM #(.bus("separate")) ram_1 (
    .addr(controlled_buffer_1_out), .din(controlled_buffer_3_out), .data(ram_1_data), .clk(not_1_out),
    .clr(in_1));  // open: str, sel, ld
  assign controlled_buffer_3_out = or_5_out ? rom_1_data : 8'bz;  // Controlled_Buffer controlled_buffer_3
  assign controlled_buffer_3_out = and_19_out ? ram_1_data : 8'bz;  // Controlled_Buffer controlled_buffer_4
  Register #(.width(4)) register_2 (.D(rom_1_data[3:0]), .Q(register_2_q), .clk(not_2_out), .clr(in_1));  // open: en
  not not_2 (not_2_out, decoder_1_out0);
  not not_3 (not_3_out, clock_1_out);
  Register register_3 (.D(controlled_buffer_3_out), .Q(register_3_q), .clk(and_3_out), .clr(in_1));  // open: en
  assign controlled_buffer_3_out = and_2_out ? register_3_q : 8'bz;  // Controlled_Buffer controlled_buffer_5
  and and_2 (and_2_out, decoder_2_out0, and_17_out);
  and and_3 (and_3_out, not_3_out, decoder_2_out0, or_3_out);
  assign controlled_buffer_3_out = and_5_out ? register_4_q : 8'bz;  // Controlled_Buffer controlled_buffer_6
  Register register_4 (.D(controlled_buffer_3_out), .Q(register_4_q), .clk(and_4_out), .clr(in_1));  // open: en
  and and_4 (and_4_out, not_3_out, decoder_2_out1, or_3_out);
  and and_5 (and_5_out, decoder_2_out1, and_17_out);
  Register register_5 (.D(controlled_buffer_3_out), .Q(register_5_q), .clk(and_7_out), .clr(in_1));  // open: en
  assign controlled_buffer_3_out = and_6_out ? register_5_q : 8'bz;  // Controlled_Buffer controlled_buffer_7
  and and_6 (and_6_out, decoder_2_out2, and_17_out);
  and and_7 (and_7_out, not_3_out, decoder_2_out2, or_3_out);
  Register register_6 (
    .D(controlled_buffer_3_out), .Q({register_6_q, register_6_q_2}), .clk(or_2_out), .clr(in_1));  // open: en
  assign controlled_buffer_3_out = and_10_out ? {register_6_q, register_6_q_2} : 8'bz;  // Controlled_Buffer controlled_buffer_8
  or or_2 (or_2_out, and_9_out, and_8_out);
  and and_8 (and_8_out, not_3_out, and_22_out);
  and and_9 (and_9_out, not_3_out, decoder_2_out3, or_3_out);
  and and_10 (and_10_out, or_6_out, and_17_out);
  or or_3 (or_3_out, and_11_out, and_19_out);
  or or_4 (or_4_out, and_15_out, and_13_out, and_20_out);
  buf or_5 (or_5_out, and_11_out);  // OR_Gate
  or or_6 (or_6_out, and_19_out, and_17_out, and_19_out);
  Decoder #(.select(4)) decoder_3 (
    .out0(decoder_3_out0), .out1(decoder_3_out1), .out2(decoder_3_out2), .out3(decoder_3_out3),
    .out4(decoder_3_out4), .out5(decoder_3_out5), .out6(decoder_3_out6), .out7(decoder_3_out7),
    .sel(register_2_q));  // open: out8, out9, out10, out11, out12, out13, out14, out15, en
  and and_11 (and_11_out, decoder_1_out2, decoder_3_out0);
  and and_12 (and_12_out, clock_1_out, and_15_out);
  or or_7 (or_7_out, and_12_out, and_21_out, and_16_out);
  and and_13 (and_13_out, decoder_1_out1, decoder_3_out1);
  and and_14 (and_14_out, decoder_1_out2, decoder_3_out1);
  and and_15 (and_15_out, decoder_1_out1, decoder_3_out0);
  and and_16 (and_16_out, clock_1_out, and_13_out);
  and and_17 (and_17_out, clock_1_out, and_14_out);
  Register register_7 (.D(rom_1_data), .Q(register_7_q), .clk(and_26_out), .clr(in_1));  // open: en
  Hex_Digit_Display hex_digit_display_1 (.value(register_6_q_2));  // open: dp
  // AND_Gate and_18 has open pins: in0=decoder_1_out2, in1=decoder_3_out3, out=open
  and and_19 (and_19_out, decoder_1_out2, decoder_3_out2);
  and and_20 (and_20_out, decoder_1_out1, decoder_3_out2);
  and and_21 (and_21_out, clock_1_out, and_20_out);
  ALU_8bit alu_8bit_1 (
    .A0(register_4_q[0]), .A1(register_4_q[1]), .A2(register_4_q[2]), .A3(register_4_q[3]),
    .A4(register_4_q[4]), .A5(register_4_q[5]), .A6(register_4_q[6]), .A7(register_4_q[7]),
    .B0(register_5_q[0]), .B1(register_5_q[1]), .B2(register_5_q[2]), .B3(register_5_q[3]),
    .B4(register_5_q[4]), .B5(register_5_q[5]), .B6(register_5_q[6]), .B7(register_5_q[7]),
    .O0(register_7_q[0]), .O1(register_7_q[1]), .O2(register_7_q[2]), .O3(register_7_q[3]),
    .C0(alu_8bit_1_c0[0]), .C1(alu_8bit_1_c0[1]), .C2(alu_8bit_1_c0[2]), .C3(alu_8bit_1_c0[3]),
    .C4(alu_8bit_1_c0[4]), .C5(alu_8bit_1_c0[5]), .C6(alu_8bit_1_c0[6]), .C7(alu_8bit_1_c0[7]));
  assign controlled_buffer_3_out = and_22_out ? alu_8bit_1_c0 : 8'bz;  // Controlled_Buffer controlled_buffer_9
  and and_22 (and_22_out, decoder_1_out2, decoder_3_out4);
  // AND_Gate and_23 has open pins: in0=decoder_1_out1, in1=decoder_3_out3, out=open
  // AND_Gate and_24 has open pins: in0=decoder_1_out1, in1=decoder_3_out5, out=open
  // AND_Gate and_25 has open pins: in0=decoder_1_out2, in1=decoder_3_out5, out=open
  and and_26 (and_26_out, decoder_1_out1, decoder_3_out4);
  // AND_Gate and_27 has open pins: in0=decoder_1_out2, in1=decoder_3_out7, out=open
  // AND_Gate and_28 has open pins: in0=decoder_1_out1, in1=decoder_3_out6, out=open
  // AND_Gate and_29 has open pins: in0=decoder_1_out2, in1=decoder_3_out6, out=open
  // AND_Gate and_30 has open pins: in0=decoder_1_out1, in1=decoder_3_out7, out=open

  // Notes on the sheet:
  //   contents of rom_1 (hex, n*v repeats v):
  //   0 1 1 4 9 0 1 3 0 2 2
endmodule

module ALU_8bit (
  input  O0,
  input  O1,
  input  A0,
  input  O2,
  input  A1,
  input  O3,
  input  A2,
  input  A3,
  input  A4,
  input  A5,
  input  A6,
  input  A7,
  input  B0,
  input  B1,
  input  B2,
  input  B3,
  input  B4,
  input  B5,
  input  B6,
  input  B7,
  output C0,
  output C1,
  output C2,
  output C3,
  output C4,
  output C5,
  output C6,
  output C7
);

  wire [7:0] adder_1_out, and_1_out, divider_1_out, multiplier_1_out, nand_1_out, nor_1_out, not_1_out,
       or_1_out, subtractor_1_out, xor_1_out;

  assign and_1_out = {A7, A6, A5, A4, A3, A2, A1, A0} & {B7, B6, B5, B4, B3, B2, B1, B0};  // AND_Gate and_1, 8 bits wide
  assign or_1_out = {A7, A6, A5, A4, A3, A2, A1, A0} | {B7, B6, B5, B4, B3, B2, B1, B0};  // OR_Gate or_1, 8 bits wide
  assign xor_1_out = {A7, A6, A5, A4, A3, A2, A1, A0} ^ {B7, B6, B5, B4, B3, B2, B1, B0};  // XOR_Gate xor_1, 8 bits wide
  assign nand_1_out = ~({A7, A6, A5, A4, A3, A2, A1, A0} & {B7, B6, B5, B4, B3, B2, B1, B0});  // NAND_Gate nand_1, 8 bits wide
  assign nor_1_out = ~({A7, A6, A5, A4, A3, A2, A1, A0} | {B7, B6, B5, B4, B3, B2, B1, B0});  // NOR_Gate nor_1, 8 bits wide
  Adder adder_1 (
    .a({A7, A6, A5, A4, A3, A2, A1, A0}), .b({B7, B6, B5, B4, B3, B2, B1, B0}), .out(adder_1_out));  // open: cin, cout
  Subtractor subtractor_1 (
    .a({A7, A6, A5, A4, A3, A2, A1, A0}), .b({B7, B6, B5, B4, B3, B2, B1, B0}), .out(subtractor_1_out));  // open: bin, bout
  Multiplier multiplier_1 (
    .a({A7, A6, A5, A4, A3, A2, A1, A0}), .b({B7, B6, B5, B4, B3, B2, B1, B0}), .out(multiplier_1_out));  // open: cin, cout
  Divider divider_1 (
    .a({A7, A6, A5, A4, A3, A2, A1, A0}), .b({B7, B6, B5, B4, B3, B2, B1, B0}), .out(divider_1_out));  // open: upper, rem
  assign not_1_out = ~{A7, A6, A5, A4, A3, A2, A1, A0};  // NOT_Gate not_1, 8 bits wide
  Multiplexer #(.select(4), .width(8)) multiplexer_1 (
    .in0({A7, A6, A5, A4, A3, A2, A1, A0}), .in1(not_1_out), .in2(and_1_out), .in3(or_1_out),
    .in4(xor_1_out), .in5(nand_1_out), .in6(nor_1_out), .in7({8{1'b1}}), .in8({8{1'b0}}), .in9(adder_1_out),
    .in10(subtractor_1_out), .in11(multiplier_1_out), .in12(divider_1_out),
    .out({C7, C6, C5, C4, C3, C2, C1, C0}), .sel({O3, O2, O1, O0}));  // open: in13, in14, in15, en
endmodule
